# Fritzing sketch CatFeederSchematic (saved by Fritzing 0.9.6b)
circuit board: 8.46667cm x 5.64444cm

parts:
  C2 = Electrolytic Capacitor [capacitance=1000μF voltage=35V package="1010 [SMD, electrolytic]"]
  C3 = Ceramic Capacitor [capacitance=100nF voltage=35V package="100 mil [THT, multilayer]"]
  S1 = Round Pushbutton
  SM1 = 28BYJ-48 Stepper Motor [part_number=28BYJ-48]
  BAT1 = 18650 Li-ion battery
  Driver1 = 28BYJ-48 Driver Module [part_number=ULN2003 package=THT]
  TP1 = TP4056 [chip_label=TP4056 package="DIP (Dual Inline) [THT]"]
  A1 = Esp32-c3 super mini
  Part2 = Adafruit MiniBoost 5V 100mA Charge Pump AP3602A [part_number=3661]

nets (from the breadboard view):
  N1: C2.+, Driver1.Vmotor, Part2.5.0V
  GND: C3.0, S1.leg1, Driver1.GND, TP1.pin6, A1.Pin_15, Part2.GND
  N2: C3.1, TP1.pin3, A1.Pin_14, Part2.VIN
  N3: S1.leg0, A1.Pin_2
  N4: SM1.blue-pin, Driver1.red-pin
  N5: SM1.pink-pin, Driver1.orange-pin
  N6: SM1.yellow-pin, Driver1.yellow-pin
  N7: SM1.orange-pin, Driver1.pink-pin
  N8: SM1.red-pin, Driver1.blue-pin
  N9: BAT1.+, TP1.pin4
  N10: BAT1.-, TP1.pin5
  N11: Driver1.IN1, A1.Pin_8
  N12: Driver1.IN2, A1.Pin_7
  N13: Driver1.IN3, A1.Pin_6
  N14: Driver1.IN4, A1.Pin_5
  N15: A1.Pin_9, Part2.!SHDN

custom parts:
  28BYJ-48 Stepper Motor: Unipolar Stepper Motor 28BYJ-48 Top coil - pink & orange Bottom coil - blue & yellow Common rail - red Connector pins: blue - pink - yellow - orange - red
  18650 Li-ion battery: Rechargable 3.7V 18650 Li-ion cell. Based on the work of Kristofer Chan.
  28BYJ-48 Driver Module: ULN2003 Driver Module for the 28BYJ-48 Unipolar Stepper Motor LED A - Blue wire - Bottom coil left LED B - Pink wire - Top coil left LED C - Yellow wire - Bottom coil right LED D - Orange wire - Top coil right Common rail - red Connector pins: blue - pink - yellow - orange - red Control pins - IN1 to IN4 Power pins - GND & Vmotor (5-12V) On/Off jumper (if removed, power to motor is cut).
  TP4056: A DIP stand-in part for whatever IC you want. With 6 pins on a 300mil dual inline package (DIP) footprint.
  Esp32-c3 super mini: ESP32-C3 Development Board ESP32 SuperMini Development Board ESP32 Development Board WiFi Bluetooth.
  Adafruit MiniBoost 5V 100mA Charge Pump AP3602A: This adorable little board will come in very handy whenever you need a small amount of 5V power. It's the size of a linear regulator, but it's actually a mini-booster! Input 3V on one side, and get 5V at up to 100mA supply on the other. Perfect for use with battery-powered projects with 2 or 3 Alkaline, or a single Lithium battery. This booster uses a charge-pump topology, which makes it very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
